# Fritzing sketch arduino_simple_motor (saved by Fritzing 0.9.3b)

parts:
  Part1 = Arduino Uno (Rev3) - ICSP
  BAT1 = BC9VPC [package=bc9vpc]
  M1 = DC Motor
  KY-1 = Relay [package=THT]

nets:
  N1: Part1.D2, KY-1.in
  N2: Part1.5V, KY-1.power
  N3: Part1.GND, KY-1.ground
  N4: BAT1.V-, M1.pin_2
  N5: M1.pin_1, KY-1.COM

notes:
  COM
  NO
  Relay Module
  DC Motor / Peristaltic Pump

custom parts:
  Relay: The Keyes 5V relay module is suitable for SCM development, home appliance control. It uses a 5V~12V TIL control signal which can control DC / AC signal.
