# Fritzing sketch rpi_8relay_test (saved by Fritzing 0.9.3b)

parts:
  8_Channel_Relay1 = 8 Channel Power Relay
  Raspberry_Pi_1 = Raspberry Pi 3 [part_number=RPI-3-V1.2]

nets:
  GND: 8_Channel_Relay1.GND, Raspberry_Pi_1.GND
  N1: 8_Channel_Relay1.IN1, Raspberry_Pi_1.GPIO2
  N2: 8_Channel_Relay1.IN2, Raspberry_Pi_1.GPIO3
  N3: 8_Channel_Relay1.IN3, Raspberry_Pi_1.GIPO4
  N4: 8_Channel_Relay1.IN4, Raspberry_Pi_1.GIPO17
  N5: 8_Channel_Relay1.IN5, Raspberry_Pi_1.GIPO27
  N6: 8_Channel_Relay1.IN6, Raspberry_Pi_1.GIPO22
  N7: 8_Channel_Relay1.IN7, Raspberry_Pi_1.GIPO10
  N8: 8_Channel_Relay1.IN8, Raspberry_Pi_1.GIPO9
  VCC: 8_Channel_Relay1.VCC, Raspberry_Pi_1.5V

custom parts:
  8 Channel Power Relay: An 8 channel power relay. The module operates at 5V.
