# Fritzing sketch rpi_liquid_mover_8pumps (saved by Fritzing 0.9.3b)
breadboards: 1

parts:
  8_Channel_Relay1 = 8 Channel Power Relay
  Raspberry_Pi_1 = Raspberry Pi 3 [part_number=RPI-3-V1.2]
  M1 = DC Motor
  LM1 = RioRand LM2596
  M2 = DC Motor
  M3 = DC Motor
  M4 = DC Motor
  M5 = DC Motor
  M6 = DC Motor
  M7 = DC Motor
  M8 = DC Motor  # not connected

nets:
  GND: 8_Channel_Relay1.GND, Raspberry_Pi_1.GND, LM1.Pin_3
  N1: 8_Channel_Relay1.IN1, Raspberry_Pi_1.GPIO2
  N2: 8_Channel_Relay1.IN2, Raspberry_Pi_1.GPIO3
  N3: 8_Channel_Relay1.IN3, Raspberry_Pi_1.GIPO4
  N4: 8_Channel_Relay1.IN4, Raspberry_Pi_1.GIPO17
  N5: 8_Channel_Relay1.IN5, Raspberry_Pi_1.GIPO27
  N6: 8_Channel_Relay1.IN6, Raspberry_Pi_1.GIPO22
  N7: 8_Channel_Relay1.IN7, Raspberry_Pi_1.GIPO10
  N8: 8_Channel_Relay1.IN8, Raspberry_Pi_1.GIPO9
  VCC: 8_Channel_Relay1.VCC, Raspberry_Pi_1.5V, LM1.Pin_2
  N9: M1.pin_2, M2.pin_2, M3.pin_2, M4.pin_2, M5.pin_2, M6.pin_2, M7.pin_2

notes:
  LM2596 Step down voltage regulator - we are using 5V for the RPi but 12V for the pumps
  DC Motors / Peristaltic Pumps
  The RPi is powered via GPIO through Pin 2 (5V) and Pin 5 (GND)
  8 channel relay module
  Universal Power Cord (3 wires)

custom parts:
  8 Channel Power Relay: An 8 channel power relay. The module operates at 5V.
